// Logisim project 16-bit processor.circ as structural Verilog: 22 circuits, main circuit main
module main (
  input  in_1,
  input  [7:0] Data,
  input  [7:0] Instruction,
  output [3:0] out_4,
  output [7:0] out_5
);

  wire clock_1_out;

  Clock clock_1 (.out(clock_1_out));
  Micro_processor micro_processor_1 (
    .Data(Data), .Instruction(Instruction), .Reset_Counter_on_1(clock_1_out), .Copy_Load(in_1),
    .Counter(out_4), .Output(out_5));
endmodule

module Full_adder (
  input  Cin,
  input  A,
  input  B,
  output Sum,
  output Cout
);

  wire and_1_out, and_2_out, xor_1_out;

  and and_1 (and_1_out, B, A);
  xor xor_1 (xor_1_out, A, B);
  and and_2 (and_2_out, xor_1_out, Cin);
  xor xor_2 (Sum, Cin, xor_1_out);
  or or_1 (Cout, and_2_out, and_1_out);
endmodule

module _4_bit_adder (
  input  Cin,
  input  [3:0] A,
  input  [3:0] B,
  output [3:0] Sum,
  output Cout
);

  wire full_adder_1_cout, full_adder_2_cout, full_adder_3_cout;

  Full_adder full_adder_1 (.A(A[0]), .B(B[0]), .Cin(Cin), .Cout(full_adder_1_cout), .Sum(Sum[0]));
  Full_adder full_adder_2 (.A(A[1]), .B(B[1]), .Cin(full_adder_1_cout), .Cout(full_adder_2_cout), .Sum(Sum[1]));
  Full_adder full_adder_3 (.A(A[2]), .B(B[2]), .Cin(full_adder_2_cout), .Cout(full_adder_3_cout), .Sum(Sum[2]));
  Full_adder full_adder_4 (.A(A[3]), .B(B[3]), .Cin(full_adder_3_cout), .Cout(Cout), .Sum(Sum[3]));
endmodule

module _4_bit_counter (
  input  Clk,
  input  Rst,
  input  Jmp,
  input  [3:0] Jmp_address,
  output [3:0] Out
);

  wire and_1_out, and_2_out, and_3_out, and_4_out, and_5_out, and_6_out, and_7_out, and_8_out, and_9_out,
       and_10_out, j_k_ff_1_qn, j_k_ff_2_qn, j_k_ff_3_qn, or_1_out, or_2_out, or_3_out, or_4_out;

  and and_1 (and_1_out, Clk, Jmp);
  and and_2 (and_2_out, Clk, Rst);
  and and_3 (and_3_out, Jmp_address[0], and_1_out);
  J_K_Flip_Flop j_k_ff_1 (
    .J(1'b1), .clk(Clk), .K(1'b1), .Q(Out[0]), .Qn(j_k_ff_1_qn), .preset(and_3_out), .reset(or_1_out));  // open: en
  or or_1 (or_1_out, and_2_out, and_4_out);
  and and_4 (and_4_out, and_1_out, ~Jmp_address[0]);  // AND_Gate
  and and_5 (and_5_out, Jmp_address[1], and_1_out);
  J_K_Flip_Flop j_k_ff_2 (
    .J(1'b1), .clk(j_k_ff_1_qn), .K(1'b1), .Q(Out[1]), .Qn(j_k_ff_2_qn), .preset(and_5_out), .reset(or_2_out));  // open: en
  or or_2 (or_2_out, and_2_out, and_6_out);
  and and_6 (and_6_out, and_1_out, ~Jmp_address[1]);  // AND_Gate
  J_K_Flip_Flop j_k_ff_3 (
    .J(1'b1), .clk(j_k_ff_2_qn), .K(1'b1), .Q(Out[2]), .Qn(j_k_ff_3_qn), .preset(and_8_out), .reset(or_3_out));  // open: en
  or or_3 (or_3_out, and_2_out, and_7_out);
  and and_7 (and_7_out, and_1_out, ~Jmp_address[2]);  // AND_Gate
  and and_8 (and_8_out, Jmp_address[2], and_1_out);
  J_K_Flip_Flop j_k_ff_4 (
    .J(1'b1), .clk(j_k_ff_3_qn), .K(1'b1), .Q(Out[3]), .preset(and_10_out), .reset(or_4_out));  // open: Qn, en
  or or_4 (or_4_out, and_2_out, and_9_out);
  and and_9 (and_9_out, and_1_out, ~Jmp_address[3]);  // AND_Gate
  and and_10 (and_10_out, Jmp_address[3], and_1_out);
endmodule

module _8_bit_adder (
  input  Cin,
  input  [7:0] in_2,
  input  [7:0] in_3,
  output [7:0] out_4,
  output Cout
);

  wire n4_bit_adder_1_cout;

  _4_bit_adder u_4_bit_adder_1 (.A(in_2[3:0]), .B(in_3[3:0]), .Cin(Cin), .Cout(n4_bit_adder_1_cout), .Sum(out_4[3:0]));
  _4_bit_adder u_4_bit_adder_2 (.A(in_2[7:4]), .B(in_3[7:4]), .Cin(n4_bit_adder_1_cout), .Cout(Cout), .Sum(out_4[7:4]));
endmodule

module _8_bit_register (
  input  Copy_Load,
  input  Clk,
  input  [7:0] Input,
  input  Rst,
  input  En,
  output [7:0] Output
);

  wire and_1_out, and_2_out;
  wire [7:0] d_ff_1_q;

  D_Flip_Flop d_ff_1 (.clk(Clk), .D(Input[0]), .Q(d_ff_1_q[0]), .en(and_1_out), .reset(Rst));  // open: Qn, preset
  D_Flip_Flop d_ff_2 (.clk(Clk), .D(Input[1]), .Q(d_ff_1_q[1]), .en(and_1_out), .reset(Rst));  // open: Qn, preset
  D_Flip_Flop d_ff_3 (.clk(Clk), .D(Input[2]), .Q(d_ff_1_q[2]), .en(and_1_out), .reset(Rst));  // open: Qn, preset
  D_Flip_Flop d_ff_4 (.clk(Clk), .D(Input[3]), .Q(d_ff_1_q[3]), .en(and_1_out), .reset(Rst));  // open: Qn, preset
  and and_1 (and_1_out, En, ~Copy_Load);  // AND_Gate
  D_Flip_Flop d_ff_5 (.clk(Clk), .D(Input[4]), .Q(d_ff_1_q[4]), .en(and_1_out), .reset(Rst));  // open: Qn, preset
  D_Flip_Flop d_ff_6 (.clk(Clk), .D(Input[5]), .Q(d_ff_1_q[5]), .en(and_1_out), .reset(Rst));  // open: Qn, preset
  D_Flip_Flop d_ff_7 (.clk(Clk), .D(Input[6]), .Q(d_ff_1_q[6]), .en(and_1_out), .reset(Rst));  // open: Qn, preset
  D_Flip_Flop d_ff_8 (.clk(Clk), .D(Input[7]), .Q(d_ff_1_q[7]), .en(and_1_out), .reset(Rst));  // open: Qn, preset
  _8_bit_gate u_8_bit_gate_1 (.in_1(d_ff_1_q), .En(and_2_out), .out_3(Output));
  and and_2 (and_2_out, En, Copy_Load);
endmodule

module _8_bit_NOT (
  input  [7:0] in_1,
  output [7:0] out_2
);

  not not_1 (out_2[0], in_1[0]);
  not not_2 (out_2[1], in_1[1]);
  not not_3 (out_2[2], in_1[2]);
  not not_4 (out_2[3], in_1[3]);
  not not_5 (out_2[4], in_1[4]);
  not not_6 (out_2[5], in_1[5]);
  not not_7 (out_2[6], in_1[6]);
  not not_8 (out_2[7], in_1[7]);
endmodule

module _8_bit_subtracter (
  input  [7:0] A,
  input  [7:0] B,
  output [7:0] Subtract,
  output Negative_value
);

  wire n8_bit_adder_1_cout;
  wire [7:0] n8_bit_adder_1_out_4, n8_bit_not_1_out_2;

  _8_bit_NOT u_8_bit_not_1 (.in_1(B), .out_2(n8_bit_not_1_out_2));
  _8_bit_adder u_8_bit_adder_1 (
    .in_2(A), .in_3(n8_bit_not_1_out_2), .Cin(1'b1), .Cout(n8_bit_adder_1_cout), .out_4(n8_bit_adder_1_out_4));
  _8_bit_gate u_8_bit_gate_1 (.in_1(n8_bit_adder_1_out_4), .En(n8_bit_adder_1_cout), .out_3(Subtract));
  not not_1 (Negative_value, n8_bit_adder_1_cout);
endmodule

module _8_bit_gate (
  input  [7:0] in_1,
  input  En,
  output [7:0] out_3
);

  and and_1 (out_3[0], in_1[0], En);
  and and_2 (out_3[1], in_1[1], En);
  and and_3 (out_3[2], in_1[2], En);
  and and_4 (out_3[3], in_1[3], En);
  and and_5 (out_3[4], in_1[4], En);
  and and_6 (out_3[5], in_1[5], En);
  and and_7 (out_3[6], in_1[6], En);
  and and_8 (out_3[7], in_1[7], En);
endmodule

module _8_bit_mux_4_to_1 (
  input  [1:0] Op,
  input  [7:0] D0,
  input  [7:0] D1,
  input  [7:0] D2,
  input  [7:0] D3,
  output [7:0] Y
);

  _4_to_1_Mux_1_bit u_4_to_1_mux_1_bit_1 (.d0(D0[0]), .d1(D1[0]), .d2(D2[0]), .d3(D3[0]), .Op(Op), .Out(Y[0]));
  _4_to_1_Mux_1_bit u_4_to_1_mux_1_bit_2 (.d0(D0[1]), .d1(D1[1]), .d2(D2[1]), .d3(D3[1]), .Op(Op), .Out(Y[1]));
  _4_to_1_Mux_1_bit u_4_to_1_mux_1_bit_3 (.d0(D0[2]), .d1(D1[2]), .d2(D2[2]), .d3(D3[2]), .Op(Op), .Out(Y[2]));
  _4_to_1_Mux_1_bit u_4_to_1_mux_1_bit_4 (.d0(D0[3]), .d1(D1[3]), .d2(D2[3]), .d3(D3[3]), .Op(Op), .Out(Y[3]));
  _4_to_1_Mux_1_bit u_4_to_1_mux_1_bit_5 (.d0(D0[4]), .d1(D1[4]), .d2(D2[4]), .d3(D3[4]), .Op(Op), .Out(Y[4]));
  _4_to_1_Mux_1_bit u_4_to_1_mux_1_bit_6 (.d0(D0[5]), .d1(D1[5]), .d2(D2[5]), .d3(D3[5]), .Op(Op), .Out(Y[5]));
  _4_to_1_Mux_1_bit u_4_to_1_mux_1_bit_7 (.d0(D0[6]), .d1(D1[6]), .d2(D2[6]), .d3(D3[6]), .Op(Op), .Out(Y[6]));
  _4_to_1_Mux_1_bit u_4_to_1_mux_1_bit_8 (.d0(D0[7]), .d1(D1[7]), .d2(D2[7]), .d3(D3[7]), .Op(Op), .Out(Y[7]));
endmodule

module _4_to_1_Mux_1_bit (
  input  [1:0] Op,
  input  d0,
  input  d1,
  input  d2,
  input  d3,
  output Out
);

  wire and_1_out, and_2_out, and_3_out, and_4_out, not_1_out, not_2_out;

  not not_1 (not_1_out, Op[0]);
  not not_2 (not_2_out, Op[1]);
  and and_1 (and_1_out, not_2_out, d0, not_1_out);
  and and_2 (and_2_out, Op[0], d1, not_2_out);
  and and_3 (and_3_out, not_1_out, d2, Op[1]);
  and and_4 (and_4_out, Op[0], d3, Op[1]);
  or or_1 (Out, and_1_out, and_2_out, and_3_out, and_4_out);
endmodule

module _8_bit_AND (
  input  [7:0] in_1,
  input  [7:0] in_2,
  output [7:0] out_3
);

  and and_1 (out_3[0], in_1[0], in_2[0]);
  and and_2 (out_3[1], in_1[1], in_2[1]);
  buf and_3 (out_3[2], in_1[2]);  // AND_Gate
  and and_4 (out_3[3], in_1[3], in_2[2]);
  and and_5 (out_3[4], in_1[4], in_2[3]);
  and and_6 (out_3[5], in_1[5], in_2[4]);
  and and_7 (out_3[6], in_1[6], in_2[5]);
  and and_8 (out_3[7], in_1[7], in_2[6]);
endmodule

module _8_bit_ALU (
  input  [1:0] Op,
  input  Clk,
  input  Cin,
  input  Copy_Load,
  input  [7:0] A,
  input  A_B,
  input  Rst,
  input  [7:0] B,
  input  Enable,
  output [7:0] Y,
  output Cout,
  output Underflow
);

  wire not_1_out, or_1_out, or_2_out;
  wire [7:0] n8_bit_adder_1_out_4, n8_bit_and_1_out_3, n8_bit_mux_4_to_1_1_y, n8_bit_not_1_out_2,
       n8_bit_register_1_output, n8_bit_register_2_output, n8_bit_subtracter_1_subtract;

  not not_1 (not_1_out, A_B);
  or or_1 (or_1_out, not_1_out, Copy_Load);
  or or_2 (or_2_out, A_B, Copy_Load);
  _8_bit_register u_8_bit_register_1 (
    .Clk(Clk), .Input(A), .Copy_Load(Copy_Load), .Rst(Rst), .En(or_1_out), .Output(n8_bit_register_1_output));
  _8_bit_register u_8_bit_register_2 (
    .Clk(Clk), .Input(B), .Copy_Load(Copy_Load), .Rst(Rst), .En(or_2_out), .Output(n8_bit_register_2_output));
  _8_bit_adder u_8_bit_adder_1 (
    .in_2(n8_bit_register_1_output), .in_3(n8_bit_register_2_output), .Cin(Cin), .Cout(Cout),
    .out_4(n8_bit_adder_1_out_4));
  _8_bit_subtracter u_8_bit_subtracter_1 (
    .A(n8_bit_register_1_output), .B(n8_bit_register_2_output), .Subtract(n8_bit_subtracter_1_subtract),
    .Negative_value(Underflow));
  _8_bit_NOT u_8_bit_not_1 (.in_1(n8_bit_register_1_output), .out_2(n8_bit_not_1_out_2));
  _8_bit_AND u_8_bit_and_1 (
    .in_1(n8_bit_register_1_output), .in_2(n8_bit_register_2_output), .out_3(n8_bit_and_1_out_3));
  _8_bit_mux_4_to_1 u_8_bit_mux_4_to_1_1 (
    .D0(n8_bit_adder_1_out_4), .D1(n8_bit_subtracter_1_subtract), .D2(n8_bit_not_1_out_2),
    .D3(n8_bit_and_1_out_3), .Op(Op), .Y(n8_bit_mux_4_to_1_1_y));
  _8_bit_gate u_8_bit_gate_1 (.in_1(n8_bit_mux_4_to_1_1_y), .En(Enable), .out_3(Y));
endmodule

module _1_to_4_demux_w_o_input (
  input  [1:0] Op,
  input  En,
  output S0,
  output S1,
  output S2,
  output S3
);

  wire not_1_out, not_2_out;

  not not_1 (not_1_out, Op[0]);
  not not_2 (not_2_out, Op[1]);
  and and_1 (S0, not_2_out, En, not_1_out);
  and and_2 (S1, Op[0], En, not_2_out);
  and and_3 (S2, not_1_out, En, Op[1]);
  and and_4 (S3, Op[0], En, Op[1]);
endmodule

module _1_to_16_demux_w_o_input (
  input  [3:0] Address,
  input  Enable,
  output out_3,
  output out_4,
  output out_5,
  output out_6,
  output out_7,
  output out_8,
  output out_9,
  output out_10,
  output out_11,
  output out_12,
  output out_13,
  output out_14,
  output out_15,
  output out_16,
  output out_17,
  output out_18
);

  wire and_1_out, and_2_out, and_3_out, and_4_out, n1_to_4_demux_w_o_input_1_s0,
       n1_to_4_demux_w_o_input_1_s1, n1_to_4_demux_w_o_input_1_s2, n1_to_4_demux_w_o_input_1_s3,
       n1_to_4_demux_w_o_input_2_s0, n1_to_4_demux_w_o_input_2_s1, n1_to_4_demux_w_o_input_2_s2,
       n1_to_4_demux_w_o_input_2_s3, n1_to_4_demux_w_o_input_3_s0, n1_to_4_demux_w_o_input_3_s1,
       n1_to_4_demux_w_o_input_3_s2, n1_to_4_demux_w_o_input_3_s3, n1_to_4_demux_w_o_input_4_s0,
       n1_to_4_demux_w_o_input_4_s1, n1_to_4_demux_w_o_input_4_s2, n1_to_4_demux_w_o_input_4_s3, not_1_out,
       not_2_out;

  not not_1 (not_1_out, Address[2]);
  not not_2 (not_2_out, Address[3]);
  and and_1 (and_1_out, not_2_out, not_1_out);
  and and_2 (and_2_out, Address[2], not_2_out);
  and and_3 (and_3_out, not_1_out, Address[3]);
  and and_4 (and_4_out, Address[2], Address[3]);
  _1_to_4_demux_w_o_input u_1_to_4_demux_w_o_input_1 (
    .En(and_1_out), .Op(Address[1:0]), .S0(n1_to_4_demux_w_o_input_1_s0), .S1(n1_to_4_demux_w_o_input_1_s1),
    .S2(n1_to_4_demux_w_o_input_1_s2), .S3(n1_to_4_demux_w_o_input_1_s3));
  _1_to_4_demux_w_o_input u_1_to_4_demux_w_o_input_2 (
    .En(and_2_out), .Op(Address[1:0]), .S0(n1_to_4_demux_w_o_input_2_s0), .S1(n1_to_4_demux_w_o_input_2_s1),
    .S2(n1_to_4_demux_w_o_input_2_s2), .S3(n1_to_4_demux_w_o_input_2_s3));
  _1_to_4_demux_w_o_input u_1_to_4_demux_w_o_input_3 (
    .En(and_3_out), .Op(Address[1:0]), .S0(n1_to_4_demux_w_o_input_3_s0), .S1(n1_to_4_demux_w_o_input_3_s1),
    .S2(n1_to_4_demux_w_o_input_3_s2), .S3(n1_to_4_demux_w_o_input_3_s3));
  _1_to_4_demux_w_o_input u_1_to_4_demux_w_o_input_4 (
    .En(and_4_out), .Op(Address[1:0]), .S0(n1_to_4_demux_w_o_input_4_s0), .S1(n1_to_4_demux_w_o_input_4_s1),
    .S2(n1_to_4_demux_w_o_input_4_s2), .S3(n1_to_4_demux_w_o_input_4_s3));
  and and_5 (out_3, n1_to_4_demux_w_o_input_1_s0, Enable);
  and and_6 (out_4, n1_to_4_demux_w_o_input_1_s1, Enable);
  and and_7 (out_5, n1_to_4_demux_w_o_input_1_s2, Enable);
  and and_8 (out_6, n1_to_4_demux_w_o_input_1_s3, Enable);
  and and_9 (out_7, n1_to_4_demux_w_o_input_2_s0, Enable);
  and and_10 (out_8, n1_to_4_demux_w_o_input_2_s1, Enable);
  and and_11 (out_9, n1_to_4_demux_w_o_input_2_s2, Enable);
  and and_12 (out_10, n1_to_4_demux_w_o_input_2_s3, Enable);
  and and_13 (out_11, n1_to_4_demux_w_o_input_3_s0, Enable);
  and and_14 (out_12, n1_to_4_demux_w_o_input_3_s1, Enable);
  and and_15 (out_13, n1_to_4_demux_w_o_input_3_s2, Enable);
  and and_16 (out_14, n1_to_4_demux_w_o_input_3_s3, Enable);
  and and_17 (out_15, n1_to_4_demux_w_o_input_4_s0, Enable);
  and and_18 (out_16, n1_to_4_demux_w_o_input_4_s1, Enable);
  and and_19 (out_17, n1_to_4_demux_w_o_input_4_s2, Enable);
  and and_20 (out_18, n1_to_4_demux_w_o_input_4_s3, Enable);
endmodule

module _16_byte_memory (
  input  Clk,
  input  Rst,
  input  [7:0] Data,
  input  Copy_load,
  input  [3:0] Address,
  input  Enable,
  output [7:0] Output
);

  wire n1_to_16_demux_w_o_input_1_out_3, n1_to_16_demux_w_o_input_1_out_4, n1_to_16_demux_w_o_input_1_out_5,
       n1_to_16_demux_w_o_input_1_out_6, n1_to_16_demux_w_o_input_1_out_7, n1_to_16_demux_w_o_input_1_out_8,
       n1_to_16_demux_w_o_input_1_out_9, n1_to_16_demux_w_o_input_1_out_10,
       n1_to_16_demux_w_o_input_1_out_11, n1_to_16_demux_w_o_input_1_out_12,
       n1_to_16_demux_w_o_input_1_out_13, n1_to_16_demux_w_o_input_1_out_14,
       n1_to_16_demux_w_o_input_1_out_15, n1_to_16_demux_w_o_input_1_out_16,
       n1_to_16_demux_w_o_input_1_out_17, n1_to_16_demux_w_o_input_1_out_18;
  wire [7:0] n8_bit_register_1_output, n8_bit_register_2_output, n8_bit_register_3_output,
       n8_bit_register_4_output, n8_bit_register_5_output, n8_bit_register_6_output,
       n8_bit_register_7_output, n8_bit_register_8_output, n8_bit_register_9_output,
       n8_bit_register_10_output, n8_bit_register_11_output, n8_bit_register_12_output,
       n8_bit_register_13_output, n8_bit_register_14_output, n8_bit_register_15_output,
       n8_bit_register_16_output, or_1_out;

  _1_to_16_demux_w_o_input u_1_to_16_demux_w_o_input_1 (
    .Address(Address), .Enable(Enable), .out_3(n1_to_16_demux_w_o_input_1_out_3),
    .out_4(n1_to_16_demux_w_o_input_1_out_4), .out_5(n1_to_16_demux_w_o_input_1_out_5),
    .out_6(n1_to_16_demux_w_o_input_1_out_6), .out_7(n1_to_16_demux_w_o_input_1_out_7),
    .out_8(n1_to_16_demux_w_o_input_1_out_8), .out_9(n1_to_16_demux_w_o_input_1_out_9),
    .out_10(n1_to_16_demux_w_o_input_1_out_10), .out_11(n1_to_16_demux_w_o_input_1_out_11),
    .out_12(n1_to_16_demux_w_o_input_1_out_12), .out_13(n1_to_16_demux_w_o_input_1_out_13),
    .out_14(n1_to_16_demux_w_o_input_1_out_14), .out_15(n1_to_16_demux_w_o_input_1_out_15),
    .out_16(n1_to_16_demux_w_o_input_1_out_16), .out_17(n1_to_16_demux_w_o_input_1_out_17),
    .out_18(n1_to_16_demux_w_o_input_1_out_18));
  _8_bit_register u_8_bit_register_1 (
    .Clk(Clk), .Input(Data), .Copy_Load(Copy_load), .Rst(Rst), .En(n1_to_16_demux_w_o_input_1_out_3),
    .Output(n8_bit_register_1_output));
  _8_bit_register u_8_bit_register_2 (
    .Clk(Clk), .Input(Data), .Copy_Load(Copy_load), .Rst(Rst), .En(n1_to_16_demux_w_o_input_1_out_7),
    .Output(n8_bit_register_2_output));
  _8_bit_register u_8_bit_register_3 (
    .Clk(Clk), .Input(Data), .Copy_Load(Copy_load), .Rst(Rst), .En(n1_to_16_demux_w_o_input_1_out_11),
    .Output(n8_bit_register_3_output));
  _8_bit_register u_8_bit_register_4 (
    .Clk(Clk), .Input(Data), .Copy_Load(Copy_load), .Rst(Rst), .En(n1_to_16_demux_w_o_input_1_out_15),
    .Output(n8_bit_register_4_output));
  _8_bit_register u_8_bit_register_5 (
    .Clk(Clk), .Input(Data), .Copy_Load(Copy_load), .Rst(Rst), .En(n1_to_16_demux_w_o_input_1_out_4),
    .Output(n8_bit_register_5_output));
  _8_bit_register u_8_bit_register_6 (
    .Clk(Clk), .Input(Data), .Copy_Load(Copy_load), .Rst(Rst), .En(n1_to_16_demux_w_o_input_1_out_8),
    .Output(n8_bit_register_6_output));
  _8_bit_register u_8_bit_register_7 (
    .Clk(Clk), .Input(Data), .Copy_Load(Copy_load), .Rst(Rst), .En(n1_to_16_demux_w_o_input_1_out_12),
    .Output(n8_bit_register_7_output));
  _8_bit_register u_8_bit_register_8 (
    .Clk(Clk), .Input(Data), .Copy_Load(Copy_load), .Rst(Rst), .En(n1_to_16_demux_w_o_input_1_out_16),
    .Output(n8_bit_register_8_output));
  _8_bit_register u_8_bit_register_9 (
    .Clk(Clk), .Input(Data), .Copy_Load(Copy_load), .Rst(Rst), .En(n1_to_16_demux_w_o_input_1_out_5),
    .Output(n8_bit_register_9_output));
  _8_bit_register u_8_bit_register_10 (
    .Clk(Clk), .Input(Data), .Copy_Load(Copy_load), .Rst(Rst), .En(n1_to_16_demux_w_o_input_1_out_9),
    .Output(n8_bit_register_10_output));
  _8_bit_register u_8_bit_register_11 (
    .Clk(Clk), .Input(Data), .Copy_Load(Copy_load), .Rst(Rst), .En(n1_to_16_demux_w_o_input_1_out_13),
    .Output(n8_bit_register_11_output));
  _8_bit_register u_8_bit_register_12 (
    .Clk(Clk), .Input(Data), .Copy_Load(Copy_load), .Rst(Rst), .En(n1_to_16_demux_w_o_input_1_out_17),
    .Output(n8_bit_register_12_output));
  assign or_1_out = n8_bit_register_4_output | n8_bit_register_3_output | n8_bit_register_2_output | n8_bit_register_1_output | n8_bit_register_8_output | n8_bit_register_7_output | n8_bit_register_6_output | n8_bit_register_5_output | n8_bit_register_12_output | n8_bit_register_11_output | n8_bit_register_10_output | n8_bit_register_9_output | n8_bit_register_16_output | n8_bit_register_15_output | n8_bit_register_14_output | n8_bit_register_13_output;  // OR_Gate or_1, 8 bits wide
  _8_bit_gate u_8_bit_gate_1 (.in_1(or_1_out), .En(Copy_load), .out_3(Output));
  _8_bit_register u_8_bit_register_13 (
    .Clk(Clk), .Input(Data), .Copy_Load(Copy_load), .Rst(Rst), .En(n1_to_16_demux_w_o_input_1_out_6),
    .Output(n8_bit_register_13_output));
  _8_bit_register u_8_bit_register_14 (
    .Clk(Clk), .Input(Data), .Copy_Load(Copy_load), .Rst(Rst), .En(n1_to_16_demux_w_o_input_1_out_10),
    .Output(n8_bit_register_14_output));
  _8_bit_register u_8_bit_register_15 (
    .Clk(Clk), .Input(Data), .Copy_Load(Copy_load), .Rst(Rst), .En(n1_to_16_demux_w_o_input_1_out_14),
    .Output(n8_bit_register_15_output));
  _8_bit_register u_8_bit_register_16 (
    .Clk(Clk), .Input(Data), .Copy_Load(Copy_load), .Rst(Rst), .En(n1_to_16_demux_w_o_input_1_out_18),
    .Output(n8_bit_register_16_output));
endmodule

module _8_bit_1_to_2_demux (
  input  Op,
  input  [7:0] A,
  output [7:0] out_3,
  output [7:0] out_4
);

  wire not_1_out;

  _8_bit_gate u_8_bit_gate_1 (.in_1(A), .En(not_1_out), .out_3(out_3));
  not not_1 (not_1_out, Op);
  _8_bit_gate u_8_bit_gate_2 (.in_1(A), .En(Op), .out_3(out_4));
endmodule

module Control_Matrix_p1 (
  input  [7:0] Instruction,
  output [3:0] Address,
  output A_B,
  output Copy_Load,
  output [1:0] ALU_Op,
  output Jmp,
  output Rst_ALU,
  output Output_data,
  output Load_from_input,
  output Move,
  output Enable_ALU
);

  wire xor_1_out;

  xor xor_1 (xor_1_out, Instruction[4], Instruction[5]);
  and and_1 (A_B, Instruction[4], xor_1_out);
  and and_2 (Copy_Load, xor_1_out, Instruction[5]);
  and and_3 (Jmp, Instruction[4], Instruction[5], ~Instruction[6], ~Instruction[7]);  // AND_Gate
  and and_4 (Rst_ALU, ~Instruction[4], ~Instruction[5], Instruction[6], ~Instruction[7]);  // AND_Gate
  and and_5 (Output_data, Instruction[4], ~Instruction[5], Instruction[6], ~Instruction[7]);  // AND_Gate
  and and_6 (Load_from_input, Instruction[4], Instruction[5], Instruction[6], ~Instruction[7]);  // AND_Gate
  and and_7 (Move, ~Instruction[4], ~Instruction[5], ~Instruction[6], Instruction[7]);  // AND_Gate
  not not_1 (Enable_ALU, Move);

  assign Address = Instruction[3:0];
  assign ALU_Op = Instruction[7:6];
endmodule

module Control_Matrix_large (
  input  Reset_memory,
  input  Clk,
  input  [7:0] Data_input,
  input  [7:0] Instruction,
  output [7:0] Output,
  output Jmp,
  output [3:0] Jump_Address,
  output Move,
  output Save_output
);

  wire control_matrix_p1_1_a_b, control_matrix_p1_1_copy_load, control_matrix_p1_1_enable_alu,
       control_matrix_p1_1_load_from_input, control_matrix_p1_1_rst_alu, or_1_out, xor_1_out;
  wire [1:0] control_matrix_p1_1_alu_op;
  wire [7:0] ALU_y, Input_gate_out_3, Input_selector_out_3, Input_selector_out_4, Memory_output, or_2_out;

  Control_Matrix_p1 control_matrix_p1_1 (
    .Instruction(Instruction), .Move(Move), .Enable_ALU(control_matrix_p1_1_enable_alu),
    .Output_data(Save_output), .Load_from_input(control_matrix_p1_1_load_from_input), .Address(Jump_Address),
    .A_B(control_matrix_p1_1_a_b), .Copy_Load(control_matrix_p1_1_copy_load),
    .ALU_Op(control_matrix_p1_1_alu_op), .Jmp(Jmp), .Rst_ALU(control_matrix_p1_1_rst_alu));
  _8_bit_gate Input_gate (.in_1(Data_input), .En(or_1_out), .out_3(Input_gate_out_3));
  or or_1 (or_1_out, Move, control_matrix_p1_1_load_from_input);
  assign or_2_out = ALU_y | Input_gate_out_3;  // OR_Gate or_2, 8 bits wide
  ExactlyOne xor_1 (
    .out(xor_1_out), .in0(control_matrix_p1_1_copy_load), .in1(Move),
    .in2(control_matrix_p1_1_load_from_input));
  _16_byte_memory Memory (
    .Clk(Clk), .Data(or_2_out), .Address(Jump_Address), .Rst(Reset_memory), .Copy_load(xor_1_out),
    .Enable(1'b1), .Output(Memory_output));
  _8_bit_1_to_2_demux Input_selector (
    .Op(control_matrix_p1_1_a_b), .A(Memory_output), .out_3(Input_selector_out_3),
    .out_4(Input_selector_out_4));
  _8_bit_ALU ALU (
    .Copy_Load(control_matrix_p1_1_copy_load), .A(Input_selector_out_3), .A_B(control_matrix_p1_1_a_b),
    .B(Input_selector_out_4), .Clk(Clk), .Cin(1'b0), .Op(control_matrix_p1_1_alu_op),
    .Rst(control_matrix_p1_1_rst_alu), .Enable(control_matrix_p1_1_enable_alu), .Y(ALU_y));  // open: Cout, Underflow
  _8_bit_gate Output_gate (.in_1(Memory_output), .En(Save_output), .out_3(Output));
endmodule

module Micro_processor (
  input  [7:0] Data,
  input  [7:0] Instruction,
  input  Reset_Counter_on_1,
  input  Copy_Load,
  output [3:0] Counter,
  output [7:0] Output
);

  wire clock_1_out, control_matrix_large_1_jmp, control_matrix_large_1_move,
       control_matrix_large_1_save_output, or_1_out, Reset_control_matrix_memory_out, Reset_instructions_out;
  wire [3:0] control_matrix_large_1_jump_address;
  wire [7:0] control_matrix_large_1_output, Instruction_memory_output, or_2_out;

  Clock clock_1 (.out(clock_1_out));
  Button Reset_instructions (.out(Reset_instructions_out));
  _4_bit_counter Program_Counter (
    .Clk(clock_1_out), .Rst(Reset_Counter_on_1), .Jmp(control_matrix_large_1_jmp),
    .Jmp_address(control_matrix_large_1_jump_address), .Out(Counter));
  _16_byte_memory Instruction_memory (
    .Clk(clock_1_out), .Data(Instruction), .Address(Counter), .Rst(Reset_instructions_out),
    .Copy_load(Copy_Load), .Enable(1'b1), .Output(Instruction_memory_output));
  _8_bit_register u_8_bit_register_1 (
    .Clk(clock_1_out), .Input(control_matrix_large_1_output), .Copy_Load(control_matrix_large_1_move),
    .En(or_1_out), .Output(Output));  // open: Rst
  or or_1 (or_1_out, control_matrix_large_1_move, control_matrix_large_1_save_output);
  Button Reset_control_matrix_memory (.out(Reset_control_matrix_memory_out));
  assign or_2_out = Data | Output;  // OR_Gate or_2, 8 bits wide
  Control_Matrix_large control_matrix_large_1 (
    .Clk(clock_1_out), .Data_input(or_2_out), .Instruction(Instruction_memory_output),
    .Reset_memory(Reset_control_matrix_memory_out), .Move(control_matrix_large_1_move),
    .Save_output(control_matrix_large_1_save_output), .Output(control_matrix_large_1_output),
    .Jmp(control_matrix_large_1_jmp), .Jump_Address(control_matrix_large_1_jump_address));
endmodule

module _1_to_8_demux_w_o_input (
  input  [7:0] in_1
);

  _1_to_4_demux_w_o_input u_1_to_4_demux_w_o_input_1 ();  // open: En, Op, S0, S1, S2, S3
  _1_to_4_demux_w_o_input u_1_to_4_demux_w_o_input_2 ();  // open: En, Op, S0, S1, S2, S3
endmodule

module Micro_processor_organized (
  input  Reset_Control_Matrix_Memory,
  input  [7:0] Data,
  input  Reset_Counter_on_1,
  input  Reset_Instruction_Memory,
  input  [7:0] Instruction,
  input  Copy_Load,
  output [3:0] Counter,
  output [7:0] Output
);

  wire clock_1_out, Control_Matrix_jmp, Control_Matrix_move, Control_Matrix_save_output, or_2_out;
  wire [3:0] Control_Matrix_jump_address;
  wire [7:0] Data_gate_output, Instruction_memory_output, or_1_out;

  Clock clock_1 (.out(clock_1_out));
  _4_bit_counter Program_Counter (
    .Clk(clock_1_out), .Rst(Reset_Counter_on_1), .Jmp(Control_Matrix_jmp),
    .Jmp_address(Control_Matrix_jump_address), .Out(Counter));
  _16_byte_memory Instruction_memory (
    .Clk(clock_1_out), .Data(Instruction), .Address(Counter), .Rst(Reset_Instruction_Memory),
    .Copy_load(Copy_Load), .Enable(1'b1), .Output(Instruction_memory_output));
  assign or_1_out = Data | Data_gate_output;  // OR_Gate or_1, 8 bits wide
  _8_bit_register Data_gate (
    .Clk(clock_1_out), .Input(Output), .Copy_Load(Control_Matrix_move), .En(or_2_out),
    .Output(Data_gate_output));  // open: Rst
  or or_2 (or_2_out, Control_Matrix_save_output, Control_Matrix_move);
  Control_Matrix_large Control_Matrix (
    .Clk(clock_1_out), .Data_input(or_1_out), .Instruction(Instruction_memory_output),
    .Reset_memory(Reset_Control_Matrix_Memory), .Move(Control_Matrix_move),
    .Save_output(Control_Matrix_save_output), .Output(Output), .Jmp(Control_Matrix_jmp),
    .Jump_Address(Control_Matrix_jump_address));
endmodule
