// Logisim project ba.circ as structural Verilog: 22 circuits, main circuit main
module main (
  input  in_1,
  input  [7:0] in_2,
  input  in_3,
  input  in_4,
  input  [3:0] Addr_a,
  input  [3:0] Addr_b,
  input  [1:0] in_7,
  input  [3:0] Addr_c,
  input  [1:0] OP,
  input  in_10,
  input  [1:0] in_11,
  input  [7:0] in_12,
  input  [7:0] in_13,
  output [7:0] out_14,
  output [3:0] out_15,
  output [7:0] out_16,
  output [3:0] out_17,
  output [3:0] out_18,
  output [3:0] out_19,
  output [1:0] out_20
);

  wire button_1_out, clock_1_out;
  wire [3:0] n4_bit_4_to_1_mux_1_out;

  Clock clock_1 (.out(clock_1_out));
  Button button_1 (.out(button_1_out));
  _4_bit_counter u_4_bit_counter_1 (.JK(in_3), .Clk(clock_1_out), .Clr(button_1_out), .Up_counter(out_15));
  _16_byte_memory u_16_byte_memory_1 (.Address(n4_bit_4_to_1_mux_1_out), .Write_read(in_1), .Data(in_2), .Out(out_14));
  _4_bit_4_to_1_mux u_4_bit_4_to_1_mux_1 (
    ._00(Addr_a), ._01(Addr_b), ._10(Addr_c), .Op(in_7), .En(in_10), .Out(n4_bit_4_to_1_mux_1_out));  // open: _11
  _8_bit_register u_8_bit_register_1 (.Write(in_4), .Clk(clock_1_out));  // open: Input, Output
  _8_bit_register u_8_bit_register_2 (.Input(out_14), .Write(in_4), .Clk(clock_1_out), .Output(out_16));
  basic_ALU_8_bit basic_alu_8_bit_1 ();  // open: Op, A, B, Output, Carry_out
  _8_bit_register u_8_bit_register_3 ();  // open: Input, Write, Clk, Output

  assign out_17 = in_12[3:0];
  assign out_18 = in_12[7:4];
  assign out_19 = in_13[3:0];
  assign out_20 = in_13[5:4];
endmodule

module Full_adder (
  input  Carry_in,
  input  A,
  input  B,
  output Sum,
  output Carry_out
);

  wire and_1_out, and_2_out, xor_1_out;

  xor xor_1 (xor_1_out, A, B);
  xor xor_2 (Sum, xor_1_out, Carry_in);
  and and_1 (and_1_out, xor_1_out, Carry_in);
  and and_2 (and_2_out, B, A);
  or or_1 (Carry_out, and_1_out, and_2_out);
endmodule

module _2_bit_adder (
  input  [1:0] B,
  input  [1:0] A,
  input  Carry_in,
  output Carry_out,
  output [1:0] Sum
);

  wire full_adder_2_carry_out;

  Full_adder full_adder_1 (.Carry_in(full_adder_2_carry_out), .A(A[1]), .B(B[1]), .Sum(Sum[1]), .Carry_out(Carry_out));
  Full_adder full_adder_2 (.Carry_in(Carry_in), .A(A[0]), .B(B[0]), .Sum(Sum[0]), .Carry_out(full_adder_2_carry_out));
endmodule

module _4_bit_adder (
  input  [3:0] in_1,
  input  [3:0] in_2,
  input  in_3,
  output out_4,
  output [3:0] out_5
);

  wire n2_bit_adder_2_carry_out;

  _2_bit_adder u_2_bit_adder_1 (
    .Carry_out(out_4), .B(in_1[3:2]), .A(in_2[3:2]), .Sum(out_5[3:2]), .Carry_in(n2_bit_adder_2_carry_out));
  _2_bit_adder u_2_bit_adder_2 (
    .Carry_out(n2_bit_adder_2_carry_out), .B(in_1[1:0]), .A(in_2[1:0]), .Sum(out_5[1:0]), .Carry_in(in_3));
endmodule

module _16_bit_adder (
  input  [15:0] in_1,
  input  [15:0] in_2,
  input  in_3,
  output out_4,
  output [15:0] out_5
);

  wire n4_bit_adder_2_out_4, n4_bit_adder_3_out_4, n4_bit_adder_4_out_4;

  _4_bit_adder u_4_bit_adder_1 (
    .out_4(out_4), .in_1(in_1[15:12]), .in_2(in_2[15:12]), .out_5(out_5[15:12]), .in_3(n4_bit_adder_3_out_4));
  _4_bit_adder u_4_bit_adder_2 (
    .out_4(n4_bit_adder_2_out_4), .in_1(in_1[7:4]), .in_2(in_2[7:4]), .out_5(out_5[7:4]),
    .in_3(n4_bit_adder_4_out_4));
  _4_bit_adder u_4_bit_adder_3 (
    .out_4(n4_bit_adder_3_out_4), .in_1(in_1[11:8]), .in_2(in_2[11:8]), .out_5(out_5[11:8]),
    .in_3(n4_bit_adder_2_out_4));
  _4_bit_adder u_4_bit_adder_4 (
    .out_4(n4_bit_adder_4_out_4), .in_1(in_1[3:0]), .in_2(in_2[3:0]), .out_5(out_5[3:0]), .in_3(in_3));
endmodule

module _2_to_1_mux (
  input  Input_1,
  input  Select,
  input  Input_0,
  output out_4
);

  wire nand_1_out, nand_2_out, not_1_out;

  not not_1 (not_1_out, Select);
  nand nand_1 (nand_1_out, Input_1, Select);
  nand nand_2 (nand_2_out, not_1_out, Input_0);
  nand nand_3 (out_4, nand_1_out, nand_2_out);
endmodule

module bit_comparator (
  input  A,
  input  B,
  output A_B,
  output A__B,
  output A_B_2
);

  wire not_1_out, not_2_out;

  not not_1 (not_1_out, B);
  xnor xnor_1 (A__B, A, B);
  not not_2 (not_2_out, A);
  and and_1 (A_B, not_1_out, A);
  and and_2 (A_B_2, B, not_2_out);
endmodule

module _8_bit_NOT (
  input  [7:0] in_1,
  output [7:0] out_2
);

  assign out_2 = ~in_1;  // NOT_Gate not_1, 8 bits wide
endmodule

module _8_bit_AND (
  input  [7:0] in_1,
  input  [7:0] in_2,
  output [7:0] out_3
);

  assign out_3 = in_1 & in_2;  // AND_Gate and_1, 8 bits wide
endmodule

module _8_bit_register (
  input  [7:0] Input,
  input  Write,
  input  Clk,
  output [7:0] Output
);

  D_flip_flop d_flip_flop_1 (.Data(Input[0]), .Ena(Write), .Clk(Clk), .Q(Output[0]));  // open: Q_prime
  D_flip_flop d_flip_flop_2 (.Data(Input[1]), .Ena(Write), .Clk(Clk), .Q(Output[1]));  // open: Q_prime
  D_flip_flop d_flip_flop_3 (.Data(Input[2]), .Ena(Write), .Clk(Clk), .Q(Output[2]));  // open: Q_prime
  D_flip_flop d_flip_flop_4 (.Data(Input[3]), .Ena(Write), .Clk(Clk), .Q(Output[3]));  // open: Q_prime
  D_flip_flop d_flip_flop_5 (.Data(Input[4]), .Ena(Write), .Clk(Clk), .Q(Output[4]));  // open: Q_prime
  D_flip_flop d_flip_flop_6 (.Data(Input[5]), .Ena(Write), .Clk(Clk), .Q(Output[5]));  // open: Q_prime
  D_flip_flop d_flip_flop_7 (.Data(Input[6]), .Ena(Write), .Clk(Clk), .Q(Output[6]));  // open: Q_prime
  D_flip_flop d_flip_flop_8 (.Data(Input[7]), .Ena(Write), .Clk(Clk), .Q(Output[7]));  // open: Q_prime
endmodule

module _8_bit_OR (
  input  [7:0] in_1,
  input  [7:0] in_2,
  output [7:0] out_3
);

  assign out_3 = in_1 | in_2;  // OR_Gate or_1, 8 bits wide
endmodule

module _8_bit_adder (
  input  [7:0] A,
  input  [7:0] B,
  input  Cin,
  output Cout,
  output [7:0] Sum
);

  wire n4_bit_adder_2_out_4;

  _4_bit_adder u_4_bit_adder_1 (
    .out_4(Cout), .in_1(A[7:4]), .in_2(B[7:4]), .out_5(Sum[7:4]), .in_3(n4_bit_adder_2_out_4));
  _4_bit_adder u_4_bit_adder_2 (
    .out_4(n4_bit_adder_2_out_4), .in_1(A[3:0]), .in_2(B[3:0]), .out_5(Sum[3:0]), .in_3(Cin));
endmodule

module Mux_2_bit_4_to_1 (
  input  [1:0] _00,
  input  [1:0] _01,
  input  [1:0] _10,
  input  [1:0] _11,
  input  [1:0] Op,
  input  En,
  output [1:0] out_7
);

  wire and_1_out, and_2_out, and_3_out, and_4_out, and_5_out, and_6_out, and_7_out, and_8_out, not_1_out,
       not_2_out;

  not not_1 (not_1_out, Op[0]);
  not not_2 (not_2_out, Op[1]);
  and and_1 (and_1_out, _00[0], not_1_out, not_2_out, En);
  and and_2 (and_2_out, not_2_out, _00[1], not_1_out, En);
  and and_3 (and_3_out, Op[0], not_2_out, En, _01[0]);
  and and_4 (and_4_out, _01[1], not_2_out, Op[0], En);
  and and_5 (and_5_out, not_1_out, _10[0], Op[1], En);
  and and_6 (and_6_out, _10[1], Op[1], not_1_out, En);
  and and_7 (and_7_out, _11[0], Op[0], Op[1], En);
  and and_8 (and_8_out, _11[1], Op[1], Op[0]);
  or or_1 (out_7[0], and_1_out, and_3_out, and_5_out, and_7_out);
  or or_2 (out_7[1], and_2_out, and_4_out, and_6_out, and_8_out);
endmodule

module _8_bit_4_to_1_mux (
  input  [7:0] _00,
  input  [7:0] _01,
  input  [7:0] _10,
  input  [7:0] _11,
  input  [1:0] Op,
  input  En,
  output [7:0] out_7
);

  Mux_2_bit_4_to_1 mux_2_bit_4_to_1_1 (
    ._00(_00[1:0]), ._01(_01[1:0]), ._10(_10[1:0]), ._11(_11[1:0]), .Op(Op), .En(En), .out_7(out_7[1:0]));
  Mux_2_bit_4_to_1 mux_2_bit_4_to_1_2 (
    ._00(_00[3:2]), ._01(_01[3:2]), ._10(_10[3:2]), ._11(_11[3:2]), .Op(Op), .En(En), .out_7(out_7[3:2]));
  Mux_2_bit_4_to_1 mux_2_bit_4_to_1_3 (
    ._00(_00[5:4]), ._01(_01[5:4]), ._10(_10[5:4]), ._11(_11[5:4]), .Op(Op), .En(En), .out_7(out_7[5:4]));
  Mux_2_bit_4_to_1 mux_2_bit_4_to_1_4 (
    ._00(_00[7:6]), ._01(_01[7:6]), ._10(_10[7:6]), ._11(_11[7:6]), .Op(Op), .En(En), .out_7(out_7[7:6]));
endmodule

module basic_ALU_8_bit (
  input  [7:0] A,
  input  [7:0] B,
  input  [1:0] Op,
  output Carry_out,
  output [7:0] Output
);

  wire [7:0] n8_bit_adder_1_sum, n8_bit_and_1_out_3, n8_bit_or_1_out_3;

  _8_bit_adder u_8_bit_adder_1 (.Cout(Carry_out), .A(B), .B(A), .Sum(n8_bit_adder_1_sum), .Cin(1'b0));
  _8_bit_AND u_8_bit_and_1 (.in_1(A), .in_2(B), .out_3(n8_bit_and_1_out_3));
  _8_bit_4_to_1_mux u_8_bit_4_to_1_mux_1 (
    ._00(n8_bit_or_1_out_3), ._01(n8_bit_and_1_out_3), ._10(n8_bit_adder_1_sum), .Op(Op), .En(1'b1),
    .out_7(Output));  // open: _11
  _8_bit_OR u_8_bit_or_1 (.in_1(B), .in_2(A), .out_3(n8_bit_or_1_out_3));
endmodule

module D_flip_flop (
  input  Data,
  input  Ena,
  input  Clk,
  output Q,
  output Q_prime
);

  wire nand_1_out, nand_2_out, not_1_out;

  not not_1 (not_1_out, Data);
  nand nand_1 (nand_1_out, Data, Ena, Clk);
  nand nand_2 (nand_2_out, Clk, not_1_out, Ena);
  nand nand_3 (Q, Q_prime, nand_1_out);
  nand nand_4 (Q_prime, Q, nand_2_out);
endmodule

module JK_flip_flop (
  input  J,
  input  Clk,
  input  K,
  output Q,
  output Q_prime
);

  wire nand_1_out, nand_2_out;

  nand nand_1 (nand_1_out, J, Q_prime, Clk);
  nand nand_2 (nand_2_out, Clk, K, Q);
  nand nand_3 (Q, Q_prime, nand_1_out);
  nand nand_4 (Q_prime, Q, nand_2_out);
endmodule

module _8_bit_comparator (
  input  [7:0] A,
  input  [7:0] B,
  output A__B
);

  wire bit_comparator_1_a__b, bit_comparator_2_a__b, bit_comparator_3_a__b, bit_comparator_4_a__b,
       bit_comparator_5_a__b, bit_comparator_6_a__b, bit_comparator_7_a__b, bit_comparator_8_a__b;

  bit_comparator bit_comparator_1 (.A(A[0]), .B(B[0]), .A__B(bit_comparator_1_a__b));  // open: A_B, A_B_2
  bit_comparator bit_comparator_2 (.A(A[1]), .B(B[1]), .A__B(bit_comparator_2_a__b));  // open: A_B, A_B_2
  bit_comparator bit_comparator_3 (.A(A[2]), .B(B[2]), .A__B(bit_comparator_3_a__b));  // open: A_B, A_B_2
  bit_comparator bit_comparator_4 (.A(A[3]), .B(B[3]), .A__B(bit_comparator_4_a__b));  // open: A_B, A_B_2
  bit_comparator bit_comparator_5 (.A(A[4]), .B(B[4]), .A__B(bit_comparator_5_a__b));  // open: A_B, A_B_2
  bit_comparator bit_comparator_6 (.A(A[5]), .B(B[5]), .A__B(bit_comparator_6_a__b));  // open: A_B, A_B_2
  bit_comparator bit_comparator_7 (.A(A[6]), .B(B[6]), .A__B(bit_comparator_7_a__b));  // open: A_B, A_B_2
  bit_comparator bit_comparator_8 (.A(A[7]), .B(B[7]), .A__B(bit_comparator_8_a__b));  // open: A_B, A_B_2
  and and_1 (A__B, bit_comparator_1_a__b, bit_comparator_2_a__b, bit_comparator_3_a__b, bit_comparator_4_a__b, bit_comparator_5_a__b, bit_comparator_6_a__b, bit_comparator_7_a__b, bit_comparator_8_a__b);
endmodule

module _8bit_1_to_4_demux (
  input  [7:0] Input,
  input  Enable,
  input  [1:0] Op,
  output [7:0] _00,
  output [7:0] _01,
  output [7:0] _10,
  output [7:0] _11
);

  wire and_1_out, and_2_out, and_3_out, and_4_out, clock_1_out;

  and and_1 (and_1_out, ~Op[1], Enable, ~Op[0]);  // AND_Gate
  and and_2 (and_2_out, ~Op[1], Enable, Op[0]);  // AND_Gate
  and and_3 (and_3_out, Op[1], Enable, ~Op[0]);  // AND_Gate
  and and_4 (and_4_out, Op[1], Enable, Op[0]);
  Clock clock_1 (.out(clock_1_out));
  _8_bit_register u_8_bit_register_1 (.Input(Input), .Write(and_1_out), .Clk(clock_1_out), .Output(_00));
  _8_bit_register u_8_bit_register_2 (.Input(Input), .Write(and_2_out), .Clk(clock_1_out), .Output(_01));
  _8_bit_register u_8_bit_register_3 (.Input(Input), .Write(and_3_out), .Clk(clock_1_out), .Output(_10));
  _8_bit_register u_8_bit_register_4 (.Input(Input), .Write(and_4_out), .Clk(clock_1_out), .Output(_11));
endmodule

module _16_byte_memory (
  input  [3:0] Address,
  input  Write_read,
  input  [7:0] Data,
  output [7:0] Out
);

  wire and_1_out, and_2_out, and_3_out, and_4_out, and_5_out, and_6_out, and_7_out, and_8_out, clock_1_out;
  wire [7:0] _0_2_output, _0__00, _0__01, _0__10, _0__11, _1_2_output, _1__00, _1__01, _1__10, _1__11,
       _10_2_output, _10__00, _10__01, _10__10, _10__11, _11_2_output, _11__00, _11__01, _11__10, _11__11,
       n8_bit_4_to_1_mux_1_out_7, n8_bit_4_to_1_mux_2_out_7, n8_bit_4_to_1_mux_3_out_7,
       n8_bit_4_to_1_mux_4_out_7, n8_bit_register_1_output, n8_bit_register_2_output,
       n8_bit_register_3_output, n8_bit_register_4_output, n8_bit_register_5_output,
       n8_bit_register_6_output, n8_bit_register_7_output, n8_bit_register_8_output,
       n8_bit_register_9_output, n8_bit_register_10_output, n8_bit_register_11_output,
       n8_bit_register_12_output;

  Clock clock_1 (.out(clock_1_out));
  and and_1 (and_1_out, ~Address[2], Write_read, ~Address[3]);  // AND_Gate
  and and_2 (and_2_out, Address[2], Write_read, ~Address[3]);  // AND_Gate
  and and_3 (and_3_out, ~Address[2], Write_read, Address[3]);  // AND_Gate
  and and_4 (and_4_out, Address[2], Write_read, Address[3]);
  _8bit_1_to_4_demux _0 (
    .Input(Data), .Enable(and_1_out), .Op(Address[1:0]), ._00(_0__00), ._01(_0__01), ._10(_0__10),
    ._11(_0__11));
  _8bit_1_to_4_demux _1 (
    .Input(Data), .Enable(and_2_out), .Op(Address[1:0]), ._00(_1__00), ._01(_1__01), ._10(_1__10),
    ._11(_1__11));
  _8bit_1_to_4_demux _10 (
    .Input(Data), .Enable(and_3_out), .Op(Address[1:0]), ._00(_10__00), ._01(_10__01), ._10(_10__10),
    ._11(_10__11));
  _8bit_1_to_4_demux _11 (
    .Input(Data), .Enable(and_4_out), .Op(Address[1:0]), ._00(_11__00), ._01(_11__01), ._10(_11__10),
    ._11(_11__11));
  _8_bit_register _0_2 (.Input(_0__00), .Write(and_1_out), .Clk(clock_1_out), .Output(_0_2_output));
  _8_bit_register _1_2 (.Input(_1__00), .Write(and_2_out), .Clk(clock_1_out), .Output(_1_2_output));
  _8_bit_register _10_2 (.Input(_10__00), .Write(and_3_out), .Clk(clock_1_out), .Output(_10_2_output));
  _8_bit_register _11_2 (.Input(_11__00), .Write(and_4_out), .Clk(clock_1_out), .Output(_11_2_output));
  _8_bit_register u_8_bit_register_1 (
    .Input(_0__01), .Write(and_1_out), .Clk(clock_1_out), .Output(n8_bit_register_1_output));
  _8_bit_register u_8_bit_register_2 (
    .Input(_1__01), .Write(and_2_out), .Clk(clock_1_out), .Output(n8_bit_register_2_output));
  _8_bit_register u_8_bit_register_3 (
    .Input(_10__01), .Write(and_3_out), .Clk(clock_1_out), .Output(n8_bit_register_3_output));
  _8_bit_register u_8_bit_register_4 (
    .Input(_11__01), .Write(and_4_out), .Clk(clock_1_out), .Output(n8_bit_register_4_output));
  _8_bit_register u_8_bit_register_5 (
    .Input(_0__11), .Write(and_1_out), .Clk(clock_1_out), .Output(n8_bit_register_5_output));
  _8_bit_register u_8_bit_register_6 (
    .Input(_0__10), .Write(and_1_out), .Clk(clock_1_out), .Output(n8_bit_register_6_output));
  _8_bit_register u_8_bit_register_7 (
    .Input(_1__10), .Write(and_2_out), .Clk(clock_1_out), .Output(n8_bit_register_7_output));
  _8_bit_register u_8_bit_register_8 (
    .Input(_1__11), .Write(and_2_out), .Clk(clock_1_out), .Output(n8_bit_register_8_output));
  _8_bit_register u_8_bit_register_9 (
    .Input(_10__11), .Write(and_3_out), .Clk(clock_1_out), .Output(n8_bit_register_9_output));
  _8_bit_register u_8_bit_register_10 (
    .Input(_10__10), .Write(and_3_out), .Clk(clock_1_out), .Output(n8_bit_register_10_output));
  _8_bit_register u_8_bit_register_11 (
    .Input(_11__10), .Write(and_4_out), .Clk(clock_1_out), .Output(n8_bit_register_11_output));
  _8_bit_register u_8_bit_register_12 (
    .Input(_11__11), .Write(and_4_out), .Clk(clock_1_out), .Output(n8_bit_register_12_output));
  _8_bit_4_to_1_mux u_8_bit_4_to_1_mux_1 (
    ._00(_0_2_output), ._01(n8_bit_register_1_output), ._10(n8_bit_register_6_output),
    ._11(n8_bit_register_5_output), .Op(Address[1:0]), .En(and_5_out), .out_7(n8_bit_4_to_1_mux_1_out_7));
  _8_bit_4_to_1_mux u_8_bit_4_to_1_mux_2 (
    ._00(_1_2_output), ._01(n8_bit_register_2_output), ._10(n8_bit_register_7_output),
    ._11(n8_bit_register_8_output), .Op(Address[1:0]), .En(and_6_out), .out_7(n8_bit_4_to_1_mux_2_out_7));
  _8_bit_4_to_1_mux u_8_bit_4_to_1_mux_3 (
    ._00(_10_2_output), ._01(n8_bit_register_3_output), ._10(n8_bit_register_10_output),
    ._11(n8_bit_register_9_output), .Op(Address[1:0]), .En(and_7_out), .out_7(n8_bit_4_to_1_mux_3_out_7));
  _8_bit_4_to_1_mux u_8_bit_4_to_1_mux_4 (
    ._00(_11_2_output), ._01(n8_bit_register_4_output), ._10(n8_bit_register_11_output),
    ._11(n8_bit_register_12_output), .Op(Address[1:0]), .En(and_8_out), .out_7(n8_bit_4_to_1_mux_4_out_7));
  and and_5 (and_5_out, ~Address[2], ~Address[3]);  // AND_Gate
  and and_6 (and_6_out, Address[2], ~Address[3]);  // AND_Gate
  and and_7 (and_7_out, ~Address[2], Address[3]);  // AND_Gate
  and and_8 (and_8_out, Address[2], Address[3]);
  assign Out = n8_bit_4_to_1_mux_1_out_7 | n8_bit_4_to_1_mux_2_out_7 | n8_bit_4_to_1_mux_3_out_7 | n8_bit_4_to_1_mux_4_out_7;  // OR_Gate or_1, 8 bits wide
endmodule

module _4_bit_counter (
  input  JK,
  input  Clk,
  input  Clr,
  output [3:0] Up_counter
);

  wire and_1_out, and_2_out;

  J_K_Flip_Flop j_k_ff_1 (.J(JK), .clk(Clk), .K(JK), .Q(Up_counter[0]), .reset(Clr));  // open: Qn, preset, en
  J_K_Flip_Flop j_k_ff_2 (
    .J(Up_counter[0]), .clk(Clk), .K(Up_counter[0]), .Q(Up_counter[1]), .reset(Clr));  // open: Qn, preset, en
  and and_1 (and_1_out, Up_counter[0], Up_counter[1]);
  J_K_Flip_Flop j_k_ff_3 (
    .J(and_1_out), .clk(Clk), .K(and_1_out), .Q(Up_counter[2]), .reset(Clr));  // open: Qn, preset, en
  and and_2 (and_2_out, and_1_out, Up_counter[2]);
  J_K_Flip_Flop j_k_ff_4 (
    .J(and_2_out), .clk(Clk), .K(and_2_out), .Q(Up_counter[3]), .reset(Clr));  // open: Qn, preset, en
endmodule

module _4_bit_4_to_1_mux (
  input  [3:0] _00,
  input  [3:0] _01,
  input  [3:0] _10,
  input  [3:0] _11,
  input  [1:0] Op,
  input  En,
  output [3:0] Out
);

  Mux_2_bit_4_to_1 mux_2_bit_4_to_1_1 (
    ._00(_00[1:0]), ._01(_01[1:0]), ._10(_10[1:0]), ._11(_11[1:0]), .Op(Op), .En(En), .out_7(Out[1:0]));
  Mux_2_bit_4_to_1 mux_2_bit_4_to_1_2 (
    ._00(_00[3:2]), ._01(_01[3:2]), ._10(_10[3:2]), ._11(_11[3:2]), .Op(Op), .En(En), .out_7(Out[3:2]));
endmodule
